# Fritzing sketch attiny85-esp8266-leds (saved by Fritzing 0.9.2b)
breadboards: 1

parts:
  Parte1 = Arduino Uno (Rev3)
  U1 = ESP8266 WiFi Module [part_number=ESP8266]
  U2 = attiny85 [package=dip]
  LED2 = smd LED [color="Red (633nm)" package="1206 [SMD]"]
  LED3 = smd LED [color="Red (633nm)" package="0603 [SMD]"]

nets:
  3V3: Parte1.3V3, U1.VCC
  N1: Parte1.5V, U2.Pin_8
  GND: Parte1.GND, U1.GND, U2.Pin_4, LED2.cathode, LED3.cathode
  N2: U1.RXD, U2.Pin_5
  N3: U1.CH_PD, U2.Pin_7
  N4: U1.TXD, U2.Pin_6
  N5: U2.Pin_2, LED3.anode
  N6: U2.Pin_3, LED2.anode

custom parts:
  ESP8266 WiFi Module: Generic WiFi Module based on the ESP8266 with onboard PCB antenna and UART communications
